// Logisim project 17485964_a5q1.circ as structural Verilog: 3 circuits, main circuit main
module main (
  output [7:0] out_1,
  output [7:0] out_2
);

  wire Clock_out;
  wire [7:0] pc_1_tomux;

  Clock Clock (.out(Clock_out));
  pc pc_1 (.FromMUX(pc_1_tomux), .ToMUX(pc_1_tomux), .CLK(Clock_out), .ToROM(out_2));
  LED led_1 (.in(out_2[7]));
  LED led_2 (.in(out_2[6]));
  LED led_3 (.in(out_2[5]));
  LED led_4 (.in(out_2[4]));
  LED led_5 (.in(out_2[3]));
  LED led_6 (.in(out_2[2]));
  LED led_7 (.in(out_2[1]));
  LED led_8 (.in(out_2[0]));
  ROM rom_1 (.addr(out_2), .data(out_1));  // open: sel
  Hex_Digit_Display hex_digit_display_1 (.value(out_1[7:4]));  // open: dp
  Hex_Digit_Display hex_digit_display_2 (.value(out_1[3:0]));  // open: dp

  // Notes on the sheet:
  //   contents of rom_1 (hex, n*v repeats v):
  //   1 0 11 1 10 0 8*10 11 5*0 8*11 5*0 11 11 11 0 10 4*0 10 0 0 0 11 11 24*0 11 1 10
endmodule

module pc (
  input  [7:0] FromMUX,
  input  CLK,
  output [7:0] ToMUX,
  output [7:0] ToROM
);

  wire [7:0] four_1_out_1;

  four four_1 (.out_1(four_1_out_1));
  Register Register (.D(FromMUX), .Q(ToROM), .clk(CLK));  // open: en, clr
  Clock Clock ();  // open: out
  Adder adder_1 (.a(four_1_out_1), .b(ToROM), .out(ToMUX));  // open: cin, cout
endmodule

module four (
  output [7:0] out_1
);


  assign out_1 = 8'h4;
endmodule
