// Logisim project 17485964_a5q2.circ as structural Verilog: 4 circuits, main circuit main
module main (
  input  [7:0] Operand_1,
  input  [7:0] Operand_2,
  input  Control
);

  wire [7:0] alu_1_result;

  alu alu_1 (.Operand_1(Operand_1), .Operand_2(Operand_2), .Control(Control), .Result(alu_1_result));
  Hex_Digit_Display hex_digit_display_1 (.value(alu_1_result[7:4]));  // open: dp
  Hex_Digit_Display hex_digit_display_2 (.value(alu_1_result[3:0]));  // open: dp
endmodule

module pc (
  output [7:0] out_1
);

  wire Clock_out;
  wire [7:0] adder_1_out, four_1_out_1, rom_1_data;

  four four_1 (.out_1(four_1_out_1));
  Register Register (.D(adder_1_out), .Q(out_1), .clk(Clock_out));  // open: en, clr
  Clock Clock (.out(Clock_out));
  LED led_1 (.in(out_1[7]));
  LED led_2 (.in(out_1[6]));
  LED led_3 (.in(out_1[5]));
  LED led_4 (.in(out_1[4]));
  LED led_5 (.in(out_1[3]));
  LED led_6 (.in(out_1[2]));
  LED led_7 (.in(out_1[1]));
  LED led_8 (.in(out_1[0]));
  Adder adder_1 (.a(four_1_out_1), .b(out_1), .out(adder_1_out));  // open: cin, cout
  ROM rom_1 (.addr(out_1), .data(rom_1_data));  // open: sel
  Hex_Digit_Display hex_digit_display_1 (.value(rom_1_data[7:4]));  // open: dp
  Hex_Digit_Display hex_digit_display_2 (.value(rom_1_data[3:0]));  // open: dp

  // Notes on the sheet:
  //   contents of rom_1 (hex, n*v repeats v):
  //   1 0 11 1 10 0 8*10 11 5*0 8*11 5*0 11 11 11 0 10 4*0 10 0 0 0 11 11 24*0 11 1 10
endmodule

module four (
  output [7:0] out_1
);


  assign out_1 = 8'h4;
endmodule

module alu (
  input  [7:0] Operand_1,
  input  [7:0] Operand_2,
  input  Control,
  output [7:0] Result
);

  wire [7:0] xor_1_out;

  assign xor_1_out = Operand_2 ^ {8{Control}};  // XOR_Gate xor_1, 8 bits wide
  Adder adder_1 (.a(Operand_1), .b(xor_1_out), .out(Result), .cin(Control));  // open: cout
endmodule
