// Logisim project 17485964_a5q3.circ as structural Verilog
module pc (
  input  [7:0] FromMUX,
  input  CLK,
  output [7:0] ToMUX,
  output [7:0] ToROM
);

  wire [7:0] four_1_out_1;

  four four_1 (.out_1(four_1_out_1));
  Register Register (.D(FromMUX), .Q(ToROM), .clk(CLK));  // open: en, clr
  Clock Clock ();  // open: out
  Adder adder_1 (.a(four_1_out_1), .b(ToROM), .out(ToMUX));  // open: cin, cout
endmodule

module four (
  output [7:0] out_1
);


  assign out_1 = 8'h4;
endmodule

module alu (
  input  [7:0] Operand_1,
  input  [7:0] Operand_2,
  input  Control,
  output [7:0] Result,
  output Status
);

  wire or_1_out;
  wire [7:0] xor_1_out;

  assign xor_1_out = Operand_2 ^ {8{Control}};  // XOR_Gate xor_1, 8 bits wide
  Adder adder_1 (.a(Operand_1), .b(xor_1_out), .out(Result), .cin(Control));  // open: cout
  or or_1 (or_1_out, Result[0], Result[1], Result[2], Result[3], Result[4], Result[5], Result[6], Result[7]);
  not not_1 (Status, or_1_out);
endmodule

// r_f
module reg_file (
  input  [7:0] WriteData,
  input  [1:0] WriteReg,
  input  [1:0] ReadReg1,
  input  [1:0] ReadReg2,
  input  RegWrite,
  input  Clock,
  output [7:0] ReadData1,
  output [7:0] ReadData2
);

  wire and_1_out, and_2_out, and_3_out, decoder_1_out1, decoder_1_out2, decoder_1_out3;
  wire [7:0] multiplexer_1_out, multiplexer_2_out, multiplexer_3_out, register_1_q, register_2_q,
       register_3_q, register_4_q;

  Decoder #(.select(2), .enable("false")) decoder_1 (
    .out1(decoder_1_out1), .out2(decoder_1_out2), .out3(decoder_1_out3), .sel(WriteReg));  // open: out0
  and and_1 (and_1_out, decoder_1_out1, RegWrite);
  and and_2 (and_2_out, decoder_1_out2, RegWrite);
  and and_3 (and_3_out, decoder_1_out3, RegWrite);
  Multiplexer #(.width(8), .enable("false")) multiplexer_1 (
    .in0(register_2_q), .in1(WriteData), .out(multiplexer_1_out), .sel(and_1_out));
  Multiplexer #(.width(8), .enable("false")) multiplexer_2 (
    .in0(register_3_q), .in1(WriteData), .out(multiplexer_2_out), .sel(and_2_out));
  Multiplexer #(.width(8), .enable("false")) multiplexer_3 (
    .in0(register_4_q), .in1(WriteData), .out(multiplexer_3_out), .sel(and_3_out));
  Register register_1 (.Q(register_1_q), .clk(Clock));  // open: D, en, clr
  Register register_2 (.D(multiplexer_1_out), .Q(register_2_q), .clk(Clock));  // open: en, clr
  Register register_3 (.D(multiplexer_2_out), .Q(register_3_q), .clk(Clock));  // open: en, clr
  Register register_4 (.D(multiplexer_3_out), .Q(register_4_q), .clk(Clock));  // open: en, clr
  Multiplexer #(.select(2), .width(8), .enable("false")) multiplexer_4 (
    .in0(register_1_q), .in1(register_2_q), .in2(register_3_q), .in3(register_4_q), .out(ReadData1),
    .sel(ReadReg1));
  Multiplexer #(.select(2), .width(8), .enable("false")) multiplexer_5 (
    .in0(register_1_q), .in1(register_2_q), .in2(register_3_q), .in3(register_4_q), .out(ReadData2),
    .sel(ReadReg2));

  // Notes on the sheet:
  //   Register File 8x8-bits
endmodule

module mini_mips (
);

  wire clock_1_out, control_1_alucontrol, control_1_alusrc, control_1_memread, control_1_memtoreg,
       control_1_memwrite, control_1_regdst, control_1_regwrite;
  wire [1:0] multiplexer_1_out;
  wire [7:0] alu_1_result, bit_extender_1_out, multiplexer_2_out, multiplexer_3_out, multiplexer_4_out,
       pc_1_tomux, pc_1_torom, ram_1_data, reg_file_1_readdata1, reg_file_1_readdata2, rom_1_data;

  pc pc_1 (.FromMUX(pc_1_tomux), .ToMUX(pc_1_tomux), .CLK(clock_1_out), .ToROM(pc_1_torom));
  Clock clock_1 (.out(clock_1_out));
  ROM rom_1 (.addr(pc_1_torom), .data(rom_1_data));  // open: sel
  Multiplexer #(.width(2), .enable("false")) multiplexer_1 (
    .in0(rom_1_data[5:4]), .in1(rom_1_data[1:0]), .out(multiplexer_1_out), .sel(control_1_regdst));
  reg_file reg_file_1 (
    .WriteData(multiplexer_4_out), .WriteReg(multiplexer_1_out), .RegWrite(control_1_regwrite),
    .Clock(clock_1_out), .ReadData1(reg_file_1_readdata1), .ReadReg1(rom_1_data[3:2]),
    .ReadData2(reg_file_1_readdata2), .ReadReg2(rom_1_data[5:4]));
  assign bit_extender_1_out = {{4{1'b0}}, rom_1_data[3:0]};  // Bit_Extender bit_extender_1
  control control_1 (
    .Op1(rom_1_data[7]), .Op0(rom_1_data[6]), .RegWrite(control_1_regwrite), .MemRead(control_1_memread),
    .ALUSrc(control_1_alusrc), .MemWrite(control_1_memwrite), .ALUcontrol(control_1_alucontrol),
    .MemtoReg(control_1_memtoreg), .RegDst(control_1_regdst));
  Multiplexer #(.width(8), .enable("false")) multiplexer_2 (
    .in0(reg_file_1_readdata1), .in1({8{1'b0}}), .out(multiplexer_2_out), .sel(control_1_alusrc));
  Multiplexer #(.width(8), .enable("false")) multiplexer_3 (
    .in0(reg_file_1_readdata2), .in1(bit_extender_1_out), .out(multiplexer_3_out), .sel(control_1_alusrc));
  Multiplexer #(.width(8), .enable("false")) multiplexer_4 (
    .in0(ram_1_data), .in1(alu_1_result), .out(multiplexer_4_out), .sel(control_1_memtoreg));
  alu alu_1 (
    .Operand_1(multiplexer_2_out), .Operand_2(multiplexer_3_out), .Control(control_1_alucontrol),
    .Result(alu_1_result));  // open: Status
  RAM #(.bus("separate")) ram_1 (
    .addr(alu_1_result), .din(reg_file_1_readdata2), .data(ram_1_data), .str(control_1_memwrite),
    .clk(clock_1_out), .ld(control_1_memread));  // open: sel, clr

  // Notes on the sheet:
  //   contents of rom_1 (hex, n*v repeats v):
  //   d0 0 0 0 56 0 0 0 a1 0 0 0 5a 0 0 0 a2 0 0 0 5a 0 0 0 a3 0 0 0 1a 0 0 0 a4 0 0 0 1a 0 0 0 a5 0 0 0
  //   1a 0 0 0 a6
endmodule

module control (
  input  Op1,
  input  Op0,
  output RegWrite,
  output MemRead,
  output ALUSrc,
  output MemWrite,
  output ALUcontrol,
  output MemtoReg,
  output RegDst
);

  wire not_1_out, not_2_out, not_3_out, not_4_out;

  not not_1 (not_1_out, Op1);
  not not_2 (not_2_out, Op0);
  not not_3 (not_3_out, Op1);
  not not_4 (not_4_out, Op0);
  not not_5 (MemtoReg, Op1);
  not not_6 (RegDst, Op1);
  or or_1 (RegWrite, not_1_out, Op0);
  and and_1 (MemRead, Op1, Op0);
  and and_2 (MemWrite, Op1, not_2_out);
  and and_3 (ALUcontrol, not_3_out, not_4_out);

  assign ALUSrc = Op1;
endmodule
